// Digital circuit xor.dig as structural Verilog
module \xor  (
  input  a1,
  input  a2,
  output out
);

  wire nand_1_out, nand_2_out, not_1_out, not_2_out;

  not not_1 (not_1_out, a2);
  not not_2 (not_2_out, a1);
  nand nand_1 (nand_1_out, a1, not_1_out);
  nand nand_2 (nand_2_out, not_2_out, a2);
  nand nand_3 (out, nand_1_out, nand_2_out);
endmodule
